# Fritzing sketch RC카회로_테스트용 2개모터 (saved by Fritzing 0.9.3b)
breadboards: 1

parts:
  부품1 = Arduino Mega ADK (Rev3)
  S1 = H-Bridge with L298N
  hc-sr3 = hc-sr04
  M1 = DC Motor
  M2 = DC Motor
  M4 = DC Motor
  M3 = DC Motor
  Raspberry_Pi_1 = Raspberry Pi 3 [part_number=RPI-3-V1.2]  # not connected
  X1 = USB Connectors [package=usb-a-pcb]  # not connected
  X2 = USB Connectors [package=usb-a-pcb]
  U1 = TRANSCHIPTC5747 [package=camera_sfv24r-2st_2]  # not connected
  J1 = Piezo Speaker
  S2 = SPST Switch [package=switch-spdt-smd]
  부품2 = Bluetooth HC-06
  S3 = H-Bridge with L298N
  X3 = USB Connectors [package=usb-a-pcb]

nets:
  N1: 부품1.D19/RX1, 부품2.TXD
  N2: 부품1.D18/TX1, 부품2.RXD
  GND: 부품1.GND, S1.GND, X2.GND, J1.pin1, 부품2.GND
  N3: 부품1.D11_PWM, J1.pin2
  5V: 부품1.5V, S1.5V, 부품2.VCC, S3.5V
  N4: 부품1.D2_PWM, S1.ENB
  N5: 부품1.D3_PWM, S1.ENA
  N6: 부품1.D4_PWM, S3.ENB
  N7: 부품1.D5_PWM, S3.ENA
  N8: 부품1.D22, S1.IN1
  N9: 부품1.D23, S1.IN2
  N10: 부품1.D24, S1.IN3
  N11: 부품1.D25, S1.IN4
  N12: 부품1.D26, S3.IN1
  N13: 부품1.D28, S3.IN2
  N14: 부품1.D30, S3.IN3
  N15: 부품1.D32, S3.IN4
  N16: 부품1.D50/MISO, hc-sr3.Trig
  N17: 부품1.D51/MOSI, hc-sr3.Echo
  N18: S1.12V, S2.P
  N19: S1.M1-01, M2.pin_2
  N20: S1.M1-02, M2.pin_1
  N21: S1.M2-01, M4.pin_1
  N22: S1.M2-02, M4.pin_2
  N23: M1.pin_1, S3.M1-02
  N24: M1.pin_2, S3.M1-01
  N25: M3.pin_1, S3.M2-01
  N26: M3.pin_2, S3.M2-02
  N27: X2.VBUS, S2.S
  N28: S3.12V, X3.VBUS
  GND_2: S3.GND, X3.GND

custom parts:
  H-Bridge with L298N: h-bridge
